# Fritzing sketch LCD with RGB,Buzzer & LM35 (saved by Fritzing 0.9.3b)
breadboards: 1

parts:
  LCD1 = LCD screen
  U1 = POT [package=pot_alpha_rv16af-20]
  Part1 = Arduino Uno (Rev3) - ICSP
  R1 = Resistor [tolerance=±5% resistance=220 package="2512 [SMD]"]
  T1 = LM35 Temperature Sensor [package="TO92 [THT]"]
  J1 = Piezo Speaker
  LED1 = RGB LED (com. anode, rbg) [package="5 mm [THT]"]

nets:
  GND: LCD1.VSS, LCD1.R/W, LCD1.LED-, U1.E, Part1.GND, T1.GND, J1.pin1, LED1.common_anode
  VDD: LCD1.VDD, U1.A, Part1.5V, R1.Pin_1, T1.+Vs
  N1: LCD1.V0, U1.S
  N2: LCD1.RS, Part1.ICSP_MISO, Part1.D12/MISO
  N3: LCD1.E, Part1.D11_PWM/MOSI
  N4: LCD1.DB4, Part1.D6_PWM
  N5: LCD1.DB5, Part1.D5_PWM
  N6: LCD1.DB6, Part1.D4
  N7: LCD1.DB7, Part1.D3_PWM
  N8: LCD1.LED+, R1.Pin_0
  N9: Part1.A0, T1.Vout
  N10: Part1.D8, LED1.red_cathode
  N11: Part1.D9_PWM, LED1.blue_cathode
  N12: Part1.D10_PWM/SS, LED1.green_cathode
  N13: Part1.D7, J1.pin2

notes:
  Arduino uno
  LCD Display
  Potentiometer
  Breadboard
  Common GND
  Common 5V
  LM35
  Buzzer
  RGB
