# Fritzing sketch RGB color mixing (saved by Fritzing 0.9.3b)
breadboards: 1

parts:
  LED1 = RGB LED (com. anode, rbg) [package="5 mm [THT]"]
  Part1 = Arduino Uno (Rev3) - ICSP
  R1 = Resistor [tolerance=±5% resistance=220 package="2010 [SMD]"]
  R2 = Resistor [tolerance=±5% resistance=220 package="0805 [SMD]"]
  R3 = Resistor [tolerance=±5% resistance=220 package="0805 [SMD]"]
  S1 = Round Pushbutton
  U1 = POT [package=pot_alpha_rv16af-20]
  S2 = Round Pushbutton

nets:
  N1: LED1.red_cathode, R3.Pin_0
  N2: LED1.common_anode, Part1.GND, S1.leg1, U1.A, S2.leg1
  N3: LED1.blue_cathode, R2.Pin_0
  N4: LED1.green_cathode, R1.Pin_0
  N5: Part1.A0, U1.S
  N6: Part1.D8, R1.Pin_1
  N7: Part1.D12/MISO, R2.Pin_1
  N8: Part1.D13/SCK, R3.Pin_1
  N9: Part1.D2, S2.leg0
  N10: Part1.D7, S1.leg0
  N11: Part1.5V, U1.E

notes:
  Push Button
  POT
  RGB
  Arduino
  220ohm
