# Fritzing sketch Push Button with Buzzer & LED (saved by Fritzing 0.9.3b)
breadboards: 1

parts:
  Part1 = Arduino Uno (Rev3) - ICSP
  S2 = Round Pushbutton
  J1 = Piezo Speaker
  LED1 = LED - 5mm [color="Red (633nm)" package="5 mm [THT]"]
  R1 = Resistor [tolerance=±10% resistance=1k package="0402 [SMD]"]

nets:
  N1: Part1.D2, Part1.GND, J1.pin1, LED1.cathode, R1.Pin_0
  N2: Part1.D3_PWM, J1.pin2
  N3: Part1.D4, LED1.anode
  N4: Part1.5V, S2.leg1
  N5: S2.leg0, R1.Pin_1

notes:
  Arduino Uno
  Buzzer
  Push Button
